# Fritzing sketch automotive_voltage_indicator-01 (saved by Fritzing 0.9.3b)
perfboards: 1

parts:
  Part1 = Arduino Pro Mini (5V)
  IC1 = Voltage Regulator [package=to-220-alt]
  C4 = Tantalum Capacitor [capacitance=470µF package="100 mil [THT, tantalum]"]
  C5 = Tantalum Capacitor [capacitance=220µF package="100 mil [THT, tantalum]"]  # not connected
  R3 = Resistor [tolerance=±1% resistance=2.2k package=THT]
  R4 = Resistor [tolerance=±1% resistance=2.2k package=THT]
  R5 = Resistor [tolerance=±1% resistance=2.2k package=THT]
  R6 = Resistor [tolerance=±2% resistance=2.4k package=THT]
  R7 = Resistor [tolerance=±2% resistance=1.2k package=THT]
  R8 = Resistor [tolerance=±2% resistance=880 package=THT]
  D2 = Zener Diode [part_number=1N5231B breakdown_voltage=3.6V package="300 mil [THT]"]

nets:
  N1: Part1.GND, IC1.IN, C4.-, R7.Pin_1, D2.cathode
  N2: Part1.RAW, IC1.OUT
  N3: Part1.A0, R6.Pin_1, R7.Pin_0, R8.Pin_1
  N4: Part1.MOSI, R5.Pin_1
  N5: Part1.D10, R4.Pin_1
  N6: Part1.D9, R3.Pin_1
  N7: R8.Pin_0, D2.anode

notes:
  12V nominal
  Vehicle ground
  (Cable to battery power)
  cable to LED
  Wire key
  brown - ground
  orange - 5V
  yellow - 12V
  cyan - Analog input
  red - red LED
  green - green LED
  blue - blue LED
