# Fritzing sketch automotive_voltage_indicator (saved by Fritzing 0.9.3b)
circuit board: 8.46667cm x 5.64444cm
breadboards: 1

parts:
  Arduino_Pro_Mini_5V = Arduino Pro Mini v13
  U1 = Voltage Regulator - 5V [package="TO220 [THT]"]
  C2 = Tantalum Capacitor [capacitance=220µF package="100 mil [THT, tantalum]"]
  LED1 = RGB LED - (4 legs) [package="5 mm [THT]"]
  R1 = Resistor [tolerance=±1% resistance=2.2k package=THT]
  R2 = Resistor [tolerance=±1% resistance=2.2k package=THT]
  R3 = Resistor [tolerance=±1% resistance=2.2k package=THT]
  R4 = Resistor [tolerance=±2% resistance=2.4k package=THT]
  R5 = Resistor [tolerance=±2% resistance=1.2k package=THT]
  D1 = Zener Diode [part_number=1N5231B breakdown_voltage=3.6V package="300 mil [THT]"]
  R6 = Resistor [tolerance=±2% resistance=880 package=THT]
  C3 = Tantalum Capacitor [capacitance=470µF package="100 mil [THT, tantalum]"]

nets:
  GND: Arduino_Pro_Mini_5V.GND, U1.GND, C2.-, LED1.common_anode, C3.-
  N1: Arduino_Pro_Mini_5V.RAW, U1.output_voltage, C2.+, D1.cathode
  N2: Arduino_Pro_Mini_5V.A0, R4.Pin_1, R5.Pin_0, R6.Pin_0
  N3: Arduino_Pro_Mini_5V.D11_PWM/MOSI, R2.Pin_1
  N4: Arduino_Pro_Mini_5V.D10_PWM/SS, R3.Pin_1
  N5: Arduino_Pro_Mini_5V.D9_PWM, R1.Pin_1
  N6: U1.input_voltage, R4.Pin_0, C3.+
  N7: LED1.red_cathode, R1.Pin_0
  N8: LED1.green_cathode, R3.Pin_0
  N9: LED1.blue_cathode, R2.Pin_0
  N10: D1.anode, R6.Pin_1

notes:
  12V nominal
  Ground
  Wire key
  brown - ground
  orange - 5V
  yellow - 12V
  cyan - Analog input
  red - red LED
  green - green LED
  blue - blue LED
